// Logisim project CPU.circ as structural Verilog: 4 circuits, main circuit implementation
module implementation (
  input  [15:0] Instruction_In,
  input  ClkIn,
  output [4:0] Instruction_Address_Out,
  output [3:0] Reg0_Out,
  output [3:0] Reg1_Out,
  output [3:0] Reg2_Out,
  output [3:0] Reg3_Out,
  output [3:0] Reg4_Out,
  output [3:0] Reg5_Out,
  output [3:0] Reg6_Out,
  output [3:0] Reg7_Out,
  output [3:0] Reg8_Out,
  output [3:0] Reg9_Out,
  output [3:0] Reg10_Out,
  output [3:0] Reg11_Out,
  output [3:0] Reg12_Out,
  output [3:0] Reg13_Out,
  output [3:0] Reg14_Out,
  output [3:0] Reg15_Out
);

  wire IsIType, IsStop, multiplexer_1_out, multiplexer_4_out, RegWrite;
  wire [3:0] A_Value, ALUResult, B_Value, multiplexer_2_out, multiplexer_3_out;
  wire [4:0] adder_1_out;

  // Probe on A_Value
  // Probe on Instruction_In[15:12]
  // Probe on B_Value
  Adder #(.width(5)) adder_1 (.a(Instruction_Address_Out), .b(5'b00001), .out(adder_1_out));  // open: cin, cout
  Multiplexer #(.enable("false")) multiplexer_1 (.in0(ClkIn), .in1(1'b1), .out(multiplexer_1_out), .sel(IsStop));
  Multiplexer #(.enable("false"), .width(4)) multiplexer_2 (
    .in0(B_Value), .in1(Instruction_In[3:0]), .out(multiplexer_2_out), .sel(IsIType));
  // Probe on IsIType
  Register #(.width(5)) PC (.D(adder_1_out), .clk(multiplexer_1_out), .Q(Instruction_Address_Out));  // open: en, clr
  InstDecoder instdecoder_1 (.OpCode(Instruction_In[15:12]), .RegWrite(RegWrite), .IsIType(IsIType), .IsStop(IsStop));
  // Probe on Instruction_In[15:12]
  // Probe on Instruction_In[3:0]
  // Probe on Instruction_In[7:4]
  // Probe on Instruction_In[11:8]
  // Probe on Instruction_Address_Out
  // Probe on Instruction_In[3:0]
  // Probe on ALUResult
  ALU alu_1 (
    .OpCode(Instruction_In[15:12]), .A(A_Value), .B(multiplexer_2_out), .Result(ALUResult));  // open: IsZeroOut
  Multiplexer #(.enable("false"), .width(4)) multiplexer_3 (
    .in0(Instruction_In[3:0]), .in1(Instruction_In[3:0]), .out(multiplexer_3_out), .sel(IsIType));
  Multiplexer #(.enable("false")) multiplexer_4 (.in0(ClkIn), .in1(1'b0), .out(multiplexer_4_out), .sel(IsStop));
  RegFile regfile_1 (
    .A_Sel_In(Instruction_In[7:4]), .B_Sel_In(multiplexer_3_out), .C_Sel_In(Instruction_In[11:8]),
    .Data_In(ALUResult), .Reg_Write_In(RegWrite), .clk_in(multiplexer_4_out), .A_Out(A_Value),
    .B_Out(B_Value), .Reg0_Out(Reg0_Out), .Reg1_Out(Reg1_Out), .Reg2_Out(Reg2_Out), .Reg3_Out(Reg3_Out),
    .Reg4_Out(Reg4_Out), .Reg5_Out(Reg5_Out), .Reg6_Out(Reg6_Out), .Reg7_Out(Reg7_Out), .Reg8_Out(Reg8_Out),
    .Reg9_Out(Reg9_Out), .Reg10_Out(Reg10_Out), .Reg11_Out(Reg11_Out), .Reg12_Out(Reg12_Out),
    .Reg13_Out(Reg13_Out), .Reg14_Out(Reg14_Out), .Reg15_Out(Reg15_Out));

  // Other names for the same wires on the sheet: Clk = ClkIn; B[3:0] = Instruction_In[3:0];
  //   Immediate[3:0] = Instruction_In[3:0]; Instruction[15:0] = Instruction_In; A[3:0] = Instruction_In[7:4];
  //   C[3:0] = Instruction_In[11:8]; OpCode[3:0] = Instruction_In[15:12];
  //   Instruction_Address[4:0] = Instruction_Address_Out; Reg0[3:0] = Reg0_Out; Reg1[3:0] = Reg1_Out;
  //   Reg2[3:0] = Reg2_Out; Reg3[3:0] = Reg3_Out; Reg4[3:0] = Reg4_Out; Reg5[3:0] = Reg5_Out; Reg6[3:0] = Reg6_Out;
  //   Reg7[3:0] = Reg7_Out; Reg8[3:0] = Reg8_Out; Reg9[3:0] = Reg9_Out; Reg10[3:0] = Reg10_Out;
  //   Reg11[3:0] = Reg11_Out; Reg12[3:0] = Reg12_Out; Reg13[3:0] = Reg13_Out; Reg14[3:0] = Reg14_Out;
  //   Reg15[3:0] = Reg15_Out
endmodule

module RegFile (
  input  [3:0] A_Sel_In,
  input  [3:0] B_Sel_In,
  input  [3:0] C_Sel_In,
  input  [3:0] Data_In,
  input  Reg_Write_In,
  input  clk_in,
  output [3:0] A_Out,
  output [3:0] B_Out,
  output [3:0] Reg0_Out,
  output [3:0] Reg1_Out,
  output [3:0] Reg2_Out,
  output [3:0] Reg3_Out,
  output [3:0] Reg4_Out,
  output [3:0] Reg5_Out,
  output [3:0] Reg6_Out,
  output [3:0] Reg7_Out,
  output [3:0] Reg8_Out,
  output [3:0] Reg9_Out,
  output [3:0] Reg10_Out,
  output [3:0] Reg11_Out,
  output [3:0] Reg12_Out,
  output [3:0] Reg13_Out,
  output [3:0] Reg14_Out,
  output [3:0] Reg15_Out
);

  wire Reg_Write0, Reg_Write1, Reg_Write2, Reg_Write3, Reg_Write4, Reg_Write5, Reg_Write6, Reg_Write7,
       Reg_Write8, Reg_Write9, Reg_Write10, Reg_Write11, Reg_Write12, Reg_Write13, Reg_Write14, Reg_Write15;

  Demultiplexer #(.enable("false"), .select(4)) demultiplexer_1 (
    .out0(Reg_Write0), .out1(Reg_Write1), .out2(Reg_Write2), .out3(Reg_Write3), .out4(Reg_Write4),
    .out5(Reg_Write5), .out6(Reg_Write6), .out7(Reg_Write7), .out8(Reg_Write8), .out9(Reg_Write9),
    .out10(Reg_Write10), .out11(Reg_Write11), .out12(Reg_Write12), .out13(Reg_Write13), .out14(Reg_Write14),
    .out15(Reg_Write15), .in(Reg_Write_In), .sel(C_Sel_In));
  Register #(.width(4)) register_1 (.D(Data_In), .en(Reg_Write0), .clk(clk_in), .Q(Reg0_Out));  // open: clr
  Register #(.width(4)) register_2 (.D(Data_In), .en(Reg_Write4), .clk(clk_in), .Q(Reg4_Out));  // open: clr
  Register #(.width(4)) register_3 (.D(Data_In), .en(Reg_Write8), .clk(clk_in), .Q(Reg8_Out));  // open: clr
  Register #(.width(4)) register_4 (.D(Data_In), .en(Reg_Write12), .clk(clk_in), .Q(Reg12_Out));  // open: clr
  Register #(.width(4)) register_5 (.D(Data_In), .en(Reg_Write1), .clk(clk_in), .Q(Reg1_Out));  // open: clr
  Register #(.width(4)) register_6 (.D(Data_In), .en(Reg_Write5), .clk(clk_in), .Q(Reg5_Out));  // open: clr
  Register #(.width(4)) register_7 (.D(Data_In), .en(Reg_Write9), .clk(clk_in), .Q(Reg9_Out));  // open: clr
  Register #(.width(4)) register_8 (.D(Data_In), .en(Reg_Write13), .clk(clk_in), .Q(Reg13_Out));  // open: clr
  Register #(.width(4)) register_9 (.D(Data_In), .en(Reg_Write2), .clk(clk_in), .Q(Reg2_Out));  // open: clr
  Register #(.width(4)) register_10 (.D(Data_In), .en(Reg_Write6), .clk(clk_in), .Q(Reg6_Out));  // open: clr
  Register #(.width(4)) register_11 (.D(Data_In), .en(Reg_Write10), .clk(clk_in), .Q(Reg10_Out));  // open: clr
  Register #(.width(4)) register_12 (.D(Data_In), .en(Reg_Write14), .clk(clk_in), .Q(Reg14_Out));  // open: clr
  Register #(.width(4)) register_13 (.D(Data_In), .en(Reg_Write3), .clk(clk_in), .Q(Reg3_Out));  // open: clr
  Register #(.width(4)) register_14 (.D(Data_In), .en(Reg_Write7), .clk(clk_in), .Q(Reg7_Out));  // open: clr
  Register #(.width(4)) register_15 (.D(Data_In), .en(Reg_Write11), .clk(clk_in), .Q(Reg11_Out));  // open: clr
  Register #(.width(4)) register_16 (.D(Data_In), .en(Reg_Write15), .clk(clk_in), .Q(Reg15_Out));  // open: clr
  Multiplexer #(.enable("false"), .select(4), .width(4)) multiplexer_1 (
    .in0(Reg0_Out), .in1(Reg1_Out), .in2(Reg2_Out), .in3(Reg3_Out), .in4(Reg4_Out), .in5(Reg5_Out),
    .in6(Reg6_Out), .in7(Reg7_Out), .in8(Reg8_Out), .in9(Reg9_Out), .in10(Reg10_Out), .in11(Reg11_Out),
    .in12(Reg12_Out), .in13(Reg13_Out), .in14(Reg14_Out), .in15(Reg15_Out), .out(A_Out), .sel(A_Sel_In));
  Multiplexer #(.enable("false"), .select(4), .width(4)) multiplexer_2 (
    .in0(Reg0_Out), .in1(Reg1_Out), .in2(Reg2_Out), .in3(Reg3_Out), .in4(Reg4_Out), .in5(Reg5_Out),
    .in6(Reg6_Out), .in7(Reg7_Out), .in8(Reg8_Out), .in9(Reg9_Out), .in10(Reg10_Out), .in11(Reg11_Out),
    .in12(Reg12_Out), .in13(Reg13_Out), .in14(Reg14_Out), .in15(Reg15_Out), .out(B_Out), .sel(B_Sel_In));

  // Other names for the same wires on the sheet: A[3:0] = A_Out; A_Sel[3:0] = A_Sel_In; B[3:0] = B_Out;
  //   B_Sel[3:0] = B_Sel_In; C_Sel[3:0] = C_Sel_In; clk = clk_in; Data[3:0] = Data_In; Reg0[3:0] = Reg0_Out;
  //   Reg1[3:0] = Reg1_Out; Reg2[3:0] = Reg2_Out; Reg3[3:0] = Reg3_Out; Reg4[3:0] = Reg4_Out; Reg5[3:0] = Reg5_Out;
  //   Reg6[3:0] = Reg6_Out; Reg7[3:0] = Reg7_Out; Reg8[3:0] = Reg8_Out; Reg9[3:0] = Reg9_Out; Reg10[3:0] = Reg10_Out;
  //   Reg11[3:0] = Reg11_Out; Reg12[3:0] = Reg12_Out; Reg13[3:0] = Reg13_Out; Reg14[3:0] = Reg14_Out;
  //   Reg15[3:0] = Reg15_Out; Reg_Write = Reg_Write_In
endmodule

module ALU (
  input  [3:0] OpCode,
  input  [3:0] A,
  input  [3:0] B,
  output [3:0] Result,
  output IsZeroOut
);

  wire [3:0] adder_1_out, adder_2_out, and_1_out, and_2_out, negator_1_out, not_1_out, or_1_out, or_2_out,
       subtractor_1_out, subtractor_2_out, xor_1_out, xor_2_out;

  assign or_1_out = A | B;  // OR_Gate or_1, 4 bits wide
  assign or_2_out = A | B;  // OR_Gate or_2, 4 bits wide
  assign and_1_out = A & B;  // AND_Gate and_1, 4 bits wide
  assign xor_1_out = A ^ B;  // XOR_Gate xor_1, 4 bits wide
  assign xor_2_out = A ^ B;  // XOR_Gate xor_2, 4 bits wide
  assign and_2_out = A & B;  // AND_Gate and_2, 4 bits wide
  assign not_1_out = ~A;  // NOT_Gate not_1, 4 bits wide
  Negator #(.width(4)) negator_1 (.in(A), .out(negator_1_out));
  Adder #(.width(4)) adder_1 (.a(A), .b(B), .out(adder_1_out));  // open: cin, cout
  Adder #(.width(4)) adder_2 (.a(A), .b(B), .out(adder_2_out));  // open: cin, cout
  Subtractor #(.width(4)) subtractor_1 (.a(A), .b(B), .out(subtractor_1_out));  // open: bin, bout
  Multiplexer #(.enable("false"), .select(4), .width(4)) multiplexer_1 (
    .in2(B), .in3(A), .in4(and_2_out), .in5(and_1_out), .in6(or_1_out), .in7(or_2_out), .in8(xor_1_out),
    .in9(xor_2_out), .in10(not_1_out), .in11(negator_1_out), .in12(adder_1_out), .in13(adder_2_out),
    .in14(subtractor_1_out), .in15(subtractor_2_out), .out(Result), .sel(OpCode));  // open: in0, in1
  Subtractor #(.width(4)) subtractor_2 (.a(A), .b(B), .out(subtractor_2_out));  // open: bin, bout

  // Other names for the same wires on the sheet: ALUOp[3:0] = OpCode; ALUResult[3:0] = Result
endmodule

module InstDecoder (
  input  [3:0] OpCode,
  output RegWrite,
  output IsIType,
  output IsStop
);

  wire and_1_out, and_2_out, and_3_out, not_1_out, not_2_out, not_3_out, not_4_out;

  not not_1 (not_1_out, OpCode[3]);
  not not_2 (not_2_out, OpCode[2]);
  not not_3 (not_3_out, OpCode[1]);
  not not_4 (not_4_out, OpCode[0]);
  or or_1 (RegWrite, OpCode[1], OpCode[2], OpCode[3]);
  and and_1 (and_1_out, not_1_out, not_2_out, OpCode[1], not_4_out);
  and and_2 (and_2_out, OpCode[2], OpCode[0]);
  and and_3 (and_3_out, OpCode[3], not_3_out, OpCode[0]);
  and and_4 (IsStop, not_1_out, not_2_out, not_3_out, not_4_out);
  or or_2 (IsIType, and_1_out, and_2_out, and_3_out);
endmodule
